# Fritzing sketch SpaceInvaders_U8g2 (saved by Fritzing 0.9.3b)
breadboards: 1

parts:
  Module = Thumb Joystick
  by_Elegoo = Arduino Uno (Rev3)
  Passive_Buzzer = Piezo Speaker
  S1 = Pushbutton [package="[THT]"]
  R1 = Resistor [tolerance=±5% resistance=100 package=THT]
  1_3inch_OLED_128x64 = WaveShare 1.3inch OLED 128x64

nets:
  GND: Module.GND, by_Elegoo.GND, S1.Pin_3, S1.Pin_4, 1_3inch_OLED_128x64.GND
  N1: Module.SEL, by_Elegoo.D2
  N2: Module.HORZ, by_Elegoo.A1
  N3: Module.VERT, by_Elegoo.A0
  5V: Module.VCC, by_Elegoo.5V, 1_3inch_OLED_128x64.VCC
  N4: by_Elegoo.A2, S1.Pin_1, S1.Pin_2
  N5: by_Elegoo.D8, 1_3inch_OLED_128x64.RES
  N6: by_Elegoo.D9_PWM, R1.Pin_1
  N7: by_Elegoo.D10_PWM/SS, Passive_Buzzer.pin1
  N8: by_Elegoo.D11_PWM/MOSI, 1_3inch_OLED_128x64.DIN
  N9: by_Elegoo.D13/SCK, 1_3inch_OLED_128x64.CLK
  N10: by_Elegoo.D6_PWM, 1_3inch_OLED_128x64.CS
  N11: by_Elegoo.D7, 1_3inch_OLED_128x64.D/C
  N12: Passive_Buzzer.pin2, R1.Pin_0

notes:
  OLED Pins may vary

custom parts:
  WaveShare 1.3inch OLED 128x64: OLED Original design by Simulz (http://tsblog.simulz.kr) Corrected PCB layout by Andreas Horneffer
